# Fritzing sketch sketch (saved by Fritzing 0.9.3b)
breadboards: 1

parts:
  Componente1 = Arduino Uno (Rev3) - ICSP
  GY1 = MPU-6050 Board GY-521 [form="♀ (female)" package=THT]

nets:
  N1: Componente1.A4/SDA, GY1.pin4
  N2: Componente1.A5/SCL, GY1.pin3
  N3: Componente1.5V, GY1.pin1
  N4: Componente1.GND, GY1.pin2

custom parts:
  MPU-6050 Board GY-521: Acelerometro y Giroscopio MPU-6050 Board GY-521
